// Logisim project dff.circ as structural Verilog: 1 circuit, main circuit main
module main (
  input  S,
  input  R,
  input  D,
  input  CLK,
  input  CLK_2,
  input  D_2,
  input  in_7,
  output Q,
  output CURR,
  output PREV,
  output Q_2,
  output out_12,
  output out_13
);

  wire nand_2_out, nand_3_out, nand_4_out, nand_5_out, nand_6_out, nand_7_out, nand_8_out, nand_10_out,
       not_1_out;

  nand nand_1 (Q, S, nand_2_out);
  nand nand_2 (nand_2_out, Q, R);
  nand nand_3 (nand_3_out, D, CLK_2);
  nand nand_4 (nand_4_out, nand_3_out, CLK_2);
  not not_1 (not_1_out, CLK_2);
  not not_2 (out_13, in_7);
  nand nand_5 (nand_5_out, nand_3_out, nand_6_out);
  nand nand_6 (nand_6_out, nand_5_out, nand_4_out);
  nand nand_7 (nand_7_out, nand_5_out, not_1_out);
  nand nand_8 (nand_8_out, not_1_out, nand_6_out);
  nand nand_9 (Q_2, nand_7_out, nand_10_out);
  nand nand_10 (nand_10_out, Q_2, nand_8_out);
  D_Flip_Flop d_ff_1 (.clk(CLK), .D(D_2), .Q(out_12));  // open: Qn, preset, en, reset
endmodule
